// Logisim project Lab1_Chips.circ as structural Verilog: 1 circuit, main circuit main
module main (
  input  B,
  input  C,
  input  D,
  output F
);

  wire n7404_1_pin12, n7432_1_pin11;

  _7404 u_7404_1 (
    .pin13(B), .pin12(n7404_1_pin12));  // open: pin1, pin2, pin3, pin4, pin5, pin6, pin11, pin10, pin9, pin8
  _7432 u_7432_1 (
    .pin13(C), .pin12(n7404_1_pin12), .pin11(n7432_1_pin11));  // open: pin1, pin2, pin3, pin4, pin5, pin6, pin10, pin9, pin8
  _7408 u_7408_1 (
    .pin13(D), .pin12(n7432_1_pin11), .pin11(F));  // open: pin1, pin2, pin3, pin4, pin5, pin6, pin10, pin9, pin8
endmodule
