// Logisim project Lab1_Logic.circ as structural Verilog: 1 circuit, main circuit main
module main (
  input  B,
  input  C,
  input  D,
  output F
);

  wire not_1_out, or_1_out;

  not not_1 (not_1_out, B);
  or or_1 (or_1_out, not_1_out, C);
  and and_1 (F, or_1_out, D);

  // Notes on the sheet:
  //   F = D(B' + C)
endmodule
