// Logisim project Lab2_1.circ as structural Verilog: 1 circuit, main circuit main
module main (
  input  in_1,
  input  in_2,
  input  in_3,
  input  in_4,
  input  in_5,
  input  in_6,
  input  in_7,
  input  in_8,
  input  in_9,
  input  in_10,
  input  in_11,
  input  in_12,
  input  in_13,
  input  in_14,
  input  in_15,
  input  in_16,
  input  in_17,
  input  in_18,
  input  in_19,
  input  in_20,
  input  in_21,
  input  in_22,
  input  in_23,
  input  in_24,
  input  in_25,
  input  in_26,
  input  in_27,
  input  in_28,
  input  in_29,
  input  in_30,
  output out_31,
  output out_32,
  output out_33,
  output out_34,
  output out_35,
  output out_36
);

  wire and_1_out, and_2_out, and_3_out, and_4_out, and_5_out, and_6_out, and_7_out, and_8_out, nand_1_out,
       nand_2_out, nand_3_out, nand_4_out, nand_5_out, nand_6_out, nand_7_out, nand_8_out, nand_9_out,
       not_1_out, not_2_out, not_3_out, not_4_out, not_5_out, not_6_out, not_7_out, not_8_out, not_9_out,
       not_10_out, not_11_out, not_12_out, not_13_out, not_14_out, not_15_out, not_16_out, not_17_out,
       not_18_out, not_19_out, not_20_out, not_21_out, not_22_out, not_23_out, not_25_out, or_2_out, or_5_out;

  not not_1 (not_1_out, in_5);
  not not_2 (not_2_out, in_7);
  not not_3 (not_3_out, in_13);
  not not_4 (not_4_out, in_15);
  not not_5 (not_5_out, in_19);
  not not_6 (not_6_out, in_21);
  not not_7 (not_7_out, in_25);
  not not_8 (not_8_out, in_27);
  and and_1 (and_1_out, in_1, in_3);
  and and_2 (and_2_out, not_1_out, not_2_out);
  and and_3 (and_3_out, in_11, not_3_out);
  and and_4 (and_4_out, in_17, not_5_out);
  and and_5 (and_5_out, not_6_out, in_23);
  and and_6 (and_6_out, not_7_out, not_8_out);
  and and_7 (and_7_out, and_2_out, in_9);
  and and_8 (and_8_out, and_3_out, not_4_out);
  or or_1 (out_33, and_4_out, and_5_out);
  and and_9 (out_35, and_6_out, in_29);
  or or_2 (or_2_out, and_1_out, and_7_out);
  or or_3 (out_31, or_2_out, and_8_out);
  nand nand_1 (nand_1_out, in_2, in_4);
  not not_9 (not_9_out, in_6);
  not not_10 (not_10_out, in_8);
  not not_11 (not_11_out, in_14);
  not not_12 (not_12_out, in_16);
  not not_13 (not_13_out, in_20);
  not not_14 (not_14_out, in_22);
  not not_15 (not_15_out, in_26);
  not not_16 (not_16_out, in_28);
  not not_17 (not_17_out, nand_1_out);
  not not_18 (not_18_out, nand_2_out);
  nand nand_2 (nand_2_out, not_9_out, not_10_out);
  nand nand_3 (nand_3_out, in_12, not_11_out);
  nand nand_4 (nand_4_out, in_18, not_13_out);
  nand nand_5 (nand_5_out, not_14_out, in_24);
  nand nand_6 (nand_6_out, not_15_out, not_16_out);
  nand nand_7 (nand_7_out, not_18_out, in_10);
  not not_19 (not_19_out, nand_3_out);
  not not_20 (not_20_out, nand_4_out);
  not not_21 (not_21_out, nand_5_out);
  not not_22 (not_22_out, nand_6_out);
  not not_23 (not_23_out, nand_7_out);
  nand nand_8 (nand_8_out, not_19_out, not_12_out);
  or or_4 (out_34, not_20_out, not_21_out);
  nand nand_9 (nand_9_out, not_22_out, in_30);
  not not_24 (out_36, nand_9_out);
  not not_25 (not_25_out, nand_8_out);
  or or_5 (or_5_out, not_17_out, not_23_out);
  or or_6 (out_32, or_5_out, not_25_out);

  // Notes on the sheet:
  //   M1:
  //   M2:
  //   A:
  //   Using 2input AND:
  //   Using 2input NAND:
  //   M1:
  //   M2:
  //   A:
endmodule
