// Logisim project Lab2_2.circ as structural Verilog: 1 circuit, main circuit main
module main (
  input  in_1,
  input  in_2,
  input  in_3,
  input  in_4,
  input  in_5,
  input  in_6,
  output out_7
);

  wire and_1_out, nor_1_out, nor_2_out, nor_3_out, not_1_out, not_2_out, not_3_out, not_4_out, not_5_out;

  not not_1 (not_1_out, in_1);
  not not_2 (not_2_out, in_4);
  nor nor_1 (nor_1_out, not_1_out, in_2);
  nor nor_2 (nor_2_out, in_3, not_2_out);
  nor nor_3 (nor_3_out, in_5, in_6);
  not not_3 (not_3_out, nor_1_out);
  not not_4 (not_4_out, nor_2_out);
  not not_5 (not_5_out, nor_3_out);
  and and_1 (and_1_out, not_3_out, not_4_out);
  and and_2 (out_7, and_1_out, not_5_out);
endmodule
