// Logisim project Lab2_3.circ as structural Verilog: 1 circuit, main circuit main
module main (
  input  in_1,
  input  in_2,
  input  in_3,
  input  in_4,
  input  in_5,
  input  in_6,
  output out_7
);

  wire n7402_1_pin13, n7402_2_pin10, n7402_3_pin10, n7404_1_pin12, n7404_2_pin12, n7404_3_pin12,
       n7404_4_pin12, n7404_5_pin12, n7408_1_pin3;

  _7404 u_7404_1 (
    .pin13(in_1), .pin12(n7404_1_pin12));  // open: pin1, pin2, pin3, pin4, pin5, pin6, pin11, pin10, pin9, pin8
  _7404 u_7404_2 (
    .pin13(in_4), .pin12(n7404_2_pin12));  // open: pin1, pin2, pin3, pin4, pin5, pin6, pin11, pin10, pin9, pin8
  _7402 u_7402_1 (
    .pin13(n7402_1_pin13), .pin12(in_2), .pin11(n7404_1_pin12));  // open: pin1, pin2, pin3, pin4, pin5, pin6, pin10, pin9, pin8
  _7402 u_7402_2 (
    .pin10(n7402_2_pin10), .pin9(n7404_2_pin12), .pin8(in_3));  // open: pin1, pin2, pin3, pin4, pin5, pin6, pin13, pin12, pin11
  _7402 u_7402_3 (
    .pin10(n7402_3_pin10), .pin9(in_6), .pin8(in_5));  // open: pin1, pin2, pin3, pin4, pin5, pin6, pin13, pin12, pin11
  _7404 u_7404_3 (
    .pin13(n7402_1_pin13), .pin12(n7404_3_pin12));  // open: pin1, pin2, pin3, pin4, pin5, pin6, pin11, pin10, pin9, pin8
  _7404 u_7404_4 (
    .pin13(n7402_2_pin10), .pin12(n7404_4_pin12));  // open: pin1, pin2, pin3, pin4, pin5, pin6, pin11, pin10, pin9, pin8
  _7404 u_7404_5 (
    .pin13(n7402_3_pin10), .pin12(n7404_5_pin12));  // open: pin1, pin2, pin3, pin4, pin5, pin6, pin11, pin10, pin9, pin8
  _7408 u_7408_1 (
    .pin1(n7404_3_pin12), .pin2(n7404_4_pin12), .pin3(n7408_1_pin3));  // open: pin4, pin5, pin6, pin13, pin12, pin11, pin10, pin9, pin8
  _7408 u_7408_2 (
    .pin1(n7408_1_pin3), .pin2(n7404_5_pin12), .pin3(out_7));  // open: pin4, pin5, pin6, pin13, pin12, pin11, pin10, pin9, pin8
endmodule
