// Logisim project 4bit_Inverter.circ as structural Verilog: 1 circuit, main circuit FourBitInverter
module FourBitInverter (
  input  A3,
  input  A2,
  input  A1,
  input  A0,
  output A3invert,
  output A2invert,
  output A1invert,
  output A0invert
);

  not not_1 (A3invert, A3);
  not not_2 (A2invert, A2);
  not not_3 (A1invert, A1);
  not not_4 (A0invert, A0);
endmodule
