// Logisim project 4bit_ORer.circ as structural Verilog: 1 circuit, main circuit FourBitORer
module FourBitORer (
  input  A3,
  input  B3,
  input  A2,
  input  B2,
  input  A1,
  input  B1,
  input  A0,
  input  B0,
  output OR3,
  output OR2,
  output OR1,
  output OR0
);

  or or_1 (OR3, A3, B3);
  or or_2 (OR2, A2, B2);
  or or_3 (OR1, A1, B1);
  or or_4 (OR0, A0, B0);
endmodule
