// Logisim project 4bit_ANDer.circ as structural Verilog: 1 circuit, main circuit FourBitANDer
module FourBitANDer (
  input  A3,
  input  B3,
  input  A2,
  input  B2,
  input  A1,
  input  B1,
  input  A0,
  input  B0,
  output AND3,
  output AND2,
  output AND1,
  output AND0
);

  and and_1 (AND3, A3, B3);
  and and_2 (AND2, A2, B2);
  and and_3 (AND1, A1, B1);
  and and_4 (AND0, A0, B0);
endmodule
