// Logisim project Lab4_VSCS.circ as structural Verilog
module VSCS (
  input  X,
  input  Y,
  input  Z,
  input  [3:0] in_4,
  input  [2:0] in_5,
  output [3:0] A,
  output [3:0] ALU_Observer,
  output [3:0] B
);

  wire and_1_out, and_2_out, and_3_out, not_1_out, not_2_out, not_3_out, undriven;
  wire [2:0] Instruction_Register_q;

  Register #(.width(3)) Instruction_Register (.D(in_5), .en(1'b1), .clk(X), .Q(Instruction_Register_q), .clr(undriven));
  not not_1 (not_1_out, Instruction_Register_q[1]);
  not not_2 (not_2_out, Instruction_Register_q[0]);
  not not_3 (not_3_out, Instruction_Register_q[2]);
  and and_1 (and_1_out, Instruction_Register_q[2], not_1_out, not_2_out);
  and and_2 (and_2_out, Y, not_3_out);
  and and_3 (and_3_out, Z, not_3_out);
  Register #(.width(4)) Register_A (.D(in_4), .en(1'b1), .clk(and_2_out), .Q(A), .clr(and_1_out));
  Register #(.width(4)) Register_B (.D(ALU_Observer), .en(1'b1), .clk(and_3_out), .Q(B), .clr(and_1_out));
  fourbit_alu fourbit_alu_1 (
    .A(A), .B(B), .S(Instruction_Register_q[1:0]), .alu3(ALU_Observer[3]), .alu2(ALU_Observer[2]),
    .alu1(ALU_Observer[1]), .alu0(ALU_Observer[0]));  // open: Carry

  // Notes on the sheet:
  //   3-bit Instruction
  //   Controller
  //   Clock Cycles
  //   ALU Control
  //   4-bit Value
  //   ALU
endmodule
