// Logisim project Lab6Part1.circ as structural Verilog: 1 circuit, main circuit main
module main (
  input  T,
  input  D,
  output F,
  output S
);

  wire clock_1_out, not_1_out, not_2_out;

  not not_1 (not_1_out, T);
  Clock clock_1 (.out(clock_1_out));
  not not_2 (not_2_out, D);
  J_K_Flip_Flop JKf (.J(T), .K(not_1_out), .clk(clock_1_out), .Q(F));  // open: Qn, preset, reset
  J_K_Flip_Flop JKs (.J(D), .K(not_2_out), .clk(clock_1_out), .Q(S));  // open: Qn, preset, reset
endmodule
