// Logisim project Lab6Part2.circ as structural Verilog
module PartF (
  input  A,
  input  B,
  input  C,
  input  D,
  input  X,
  input  Y,
  output Dx,
  output Dy
);

  wire and_1_out, and_2_out, and_3_out, and_4_out, and_5_out, and_6_out, and_7_out, and_8_out, and_9_out,
       not_1_out, not_2_out, not_3_out, not_4_out, or_1_out, or_2_out, or_3_out, or_4_out, or_5_out;

  not not_1 (not_1_out, A);
  not not_2 (not_2_out, C);
  not not_3 (not_3_out, X);
  not not_4 (not_4_out, Y);
  and and_1 (and_1_out, not_1_out, not_2_out);
  and and_2 (and_2_out, A, C);
  or or_1 (or_1_out, not_2_out, A);
  or or_2 (or_2_out, A, B);
  or or_3 (or_3_out, B, C);
  or or_4 (or_4_out, and_1_out, and_2_out);
  or or_5 (or_5_out, C, D);
  and and_3 (and_3_out, not_3_out, not_4_out, or_1_out);
  and and_4 (and_4_out, X, not_4_out, or_2_out);
  and and_5 (and_5_out, X, Y, or_3_out);
  and and_6 (and_6_out, not_3_out, not_4_out, or_4_out);
  and and_7 (and_7_out, not_3_out, Y, or_5_out);
  and and_8 (and_8_out, X, not_4_out);
  and and_9 (and_9_out, X, Y, B, C);
  or or_6 (Dy, and_3_out, and_4_out, and_5_out);
  or or_7 (Dx, and_6_out, and_7_out, and_8_out, and_9_out);
endmodule
