// Logisim project Part_1.circ as structural Verilog: 1 circuit, main circuit Part_1_Register
module Part_1_Register (
  input  D0,
  input  D1,
  input  D2,
  input  D3,
  input  ENABLE,
  input  LOAD,
  input  CLOCK,
  output Q0,
  output Q1,
  output Q2,
  output Q3
);

  wire and_1_out, multiplexer_1_out, multiplexer_2_out, multiplexer_3_out, multiplexer_4_out, not_1_out,
       not_2_out, not_3_out, not_4_out;

  and and_1 (and_1_out, ENABLE, LOAD);
  Multiplexer multiplexer_1 (.in0(Q0), .in1(D0), .out(multiplexer_1_out), .sel(and_1_out));
  Multiplexer multiplexer_2 (.in0(Q1), .in1(D1), .out(multiplexer_2_out), .sel(and_1_out));
  Multiplexer multiplexer_3 (.in0(Q2), .in1(D2), .out(multiplexer_3_out), .sel(and_1_out));
  Multiplexer multiplexer_4 (.in0(Q3), .in1(D3), .out(multiplexer_4_out), .sel(and_1_out));
  J_K_Flip_Flop j_k_ff_1 (.J(multiplexer_1_out), .K(not_1_out), .clk(CLOCK), .Q(Q0));  // open: Qn, preset, reset
  not not_1 (not_1_out, multiplexer_1_out);
  J_K_Flip_Flop j_k_ff_2 (.J(multiplexer_2_out), .K(not_2_out), .clk(CLOCK), .Q(Q1));  // open: Qn, preset, reset
  not not_2 (not_2_out, multiplexer_2_out);
  J_K_Flip_Flop j_k_ff_3 (.J(multiplexer_3_out), .K(not_3_out), .clk(CLOCK), .Q(Q2));  // open: Qn, preset, reset
  not not_3 (not_3_out, multiplexer_3_out);
  J_K_Flip_Flop j_k_ff_4 (.J(multiplexer_4_out), .K(not_4_out), .clk(CLOCK), .Q(Q3));  // open: Qn, preset, reset
  not not_4 (not_4_out, multiplexer_4_out);
endmodule
