// Logisim project Part_2.circ as structural Verilog: 1 circuit, main circuit main
module main (
  input  [3:0] in_1,
  input  ENABLE_1,
  input  LOAD_1,
  input  BusTransfer_1,
  input  ENABLE_2,
  input  LOAD_2,
  input  BusTransfer_2,
  input  ENABLE_3,
  input  LOAD_3,
  input  BusTransfer_3,
  input  ENABLE_4,
  input  LOAD_4,
  input  BusTransfer_4,
  input  CLOCK,
  output [3:0] BUS_Output
);

  wire Register_1_q0, Register_1_q1, Register_1_q2, Register_1_q3, Register_2_q0, Register_2_q1,
       Register_2_q2, Register_2_q3, Register_3_q0, Register_3_q1, Register_3_q2, Register_3_q3,
       Register_4_q0, Register_4_q1, Register_4_q2, Register_4_q3;

  Part_1_Register Register_1 (
    .D0(in_1[3]), .D1(in_1[2]), .D2(in_1[1]), .D3(in_1[0]), .ENABLE(ENABLE_1), .LOAD(LOAD_1), .CLOCK(CLOCK),
    .Q0(Register_1_q0), .Q1(Register_1_q1), .Q2(Register_1_q2), .Q3(Register_1_q3));
  Part_1_Register Register_2 (
    .D0(BUS_Output[3]), .D1(BUS_Output[2]), .D2(BUS_Output[1]), .D3(BUS_Output[0]), .ENABLE(ENABLE_2),
    .LOAD(LOAD_2), .CLOCK(CLOCK), .Q0(Register_2_q0), .Q1(Register_2_q1), .Q2(Register_2_q2),
    .Q3(Register_2_q3));
  Part_1_Register Register_3 (
    .D0(BUS_Output[3]), .D1(BUS_Output[2]), .D2(BUS_Output[1]), .D3(BUS_Output[0]), .ENABLE(ENABLE_3),
    .LOAD(LOAD_3), .CLOCK(CLOCK), .Q0(Register_3_q0), .Q1(Register_3_q1), .Q2(Register_3_q2),
    .Q3(Register_3_q3));
  Part_1_Register Register_4 (
    .D0(BUS_Output[3]), .D1(BUS_Output[2]), .D2(BUS_Output[1]), .D3(BUS_Output[0]), .ENABLE(ENABLE_4),
    .LOAD(LOAD_4), .CLOCK(CLOCK), .Q0(Register_4_q0), .Q1(Register_4_q1), .Q2(Register_4_q2),
    .Q3(Register_4_q3));
  assign BUS_Output[3] = BusTransfer_1 ? Register_1_q0 : 1'bz;  // Controlled_Buffer controlled_buffer_1
  assign BUS_Output[2] = BusTransfer_1 ? Register_1_q1 : 1'bz;  // Controlled_Buffer controlled_buffer_2
  assign BUS_Output[1] = BusTransfer_1 ? Register_1_q2 : 1'bz;  // Controlled_Buffer controlled_buffer_3
  assign BUS_Output[0] = BusTransfer_1 ? Register_1_q3 : 1'bz;  // Controlled_Buffer controlled_buffer_4
  assign BUS_Output[3] = BusTransfer_2 ? Register_2_q0 : 1'bz;  // Controlled_Buffer controlled_buffer_5
  assign BUS_Output[2] = BusTransfer_2 ? Register_2_q1 : 1'bz;  // Controlled_Buffer controlled_buffer_6
  assign BUS_Output[1] = BusTransfer_2 ? Register_2_q2 : 1'bz;  // Controlled_Buffer controlled_buffer_7
  assign BUS_Output[0] = BusTransfer_2 ? Register_2_q3 : 1'bz;  // Controlled_Buffer controlled_buffer_8
  assign BUS_Output[3] = BusTransfer_3 ? Register_3_q0 : 1'bz;  // Controlled_Buffer controlled_buffer_9
  assign BUS_Output[2] = BusTransfer_3 ? Register_3_q1 : 1'bz;  // Controlled_Buffer controlled_buffer_10
  assign BUS_Output[1] = BusTransfer_3 ? Register_3_q2 : 1'bz;  // Controlled_Buffer controlled_buffer_11
  assign BUS_Output[0] = BusTransfer_3 ? Register_3_q3 : 1'bz;  // Controlled_Buffer controlled_buffer_12
  assign BUS_Output[3] = BusTransfer_4 ? Register_4_q0 : 1'bz;  // Controlled_Buffer controlled_buffer_13
  assign BUS_Output[2] = BusTransfer_4 ? Register_4_q1 : 1'bz;  // Controlled_Buffer controlled_buffer_14
  assign BUS_Output[1] = BusTransfer_4 ? Register_4_q2 : 1'bz;  // Controlled_Buffer controlled_buffer_15
  assign BUS_Output[0] = BusTransfer_4 ? Register_4_q3 : 1'bz;  // Controlled_Buffer controlled_buffer_16
endmodule
