// Logisim project 4bit_ALU.circ as structural Verilog: 1 circuit, main circuit fourbit_alu
module fourbit_alu (
  input  [3:0] A,
  input  [3:0] B,
  input  [1:0] S,
  output Carry,
  output alu3,
  output alu2,
  output alu1,
  output alu0
);

  wire fourbitadder_1_sum0, fourbitadder_1_sum1, fourbitadder_1_sum2, fourbitadder_1_sum3,
       fourbitander_1_and0, fourbitander_1_and1, fourbitander_1_and2, fourbitander_1_and3,
       fourbitinverter_1_a0invert, fourbitinverter_1_a1invert, fourbitinverter_1_a2invert,
       fourbitinverter_1_a3invert, fourbitorer_1_or0, fourbitorer_1_or1, fourbitorer_1_or2, fourbitorer_1_or3;

  FourBitAdder fourbitadder_1 (
    .A3(A[3]), .B3(B[3]), .A2(A[2]), .B2(B[2]), .A1(A[1]), .B1(B[1]), .A0(A[0]), .B0(B[0]), .Carry(Carry),
    .SUM3(fourbitadder_1_sum3), .SUM2(fourbitadder_1_sum2), .SUM1(fourbitadder_1_sum1),
    .SUM0(fourbitadder_1_sum0));
  FourBitANDer fourbitander_1 (
    .A3(A[3]), .B3(B[3]), .A2(A[2]), .B2(B[2]), .A1(A[1]), .B1(B[1]), .A0(A[0]), .B0(B[0]),
    .AND3(fourbitander_1_and3), .AND2(fourbitander_1_and2), .AND1(fourbitander_1_and1),
    .AND0(fourbitander_1_and0));
  FourBitORer fourbitorer_1 (
    .A3(A[3]), .B3(B[3]), .A2(A[2]), .B2(B[2]), .A1(A[1]), .B1(B[1]), .A0(A[0]), .B0(B[0]),
    .OR3(fourbitorer_1_or3), .OR2(fourbitorer_1_or2), .OR1(fourbitorer_1_or1), .OR0(fourbitorer_1_or0));
  FourBitInverter fourbitinverter_1 (
    .A3(A[3]), .A2(A[2]), .A1(A[1]), .A0(A[0]), .A3invert(fourbitinverter_1_a3invert),
    .A2invert(fourbitinverter_1_a2invert), .A1invert(fourbitinverter_1_a1invert),
    .A0invert(fourbitinverter_1_a0invert));
  Multiplexer #(.select(2)) multiplexer_1 (
    .in0(fourbitinverter_1_a3invert), .in1(fourbitorer_1_or3), .in2(fourbitander_1_and3),
    .in3(fourbitadder_1_sum3), .out(alu3), .sel(S));
  Multiplexer #(.select(2)) multiplexer_2 (
    .in0(fourbitinverter_1_a2invert), .in1(fourbitorer_1_or2), .in2(fourbitander_1_and2),
    .in3(fourbitadder_1_sum2), .out(alu2), .sel(S));
  Multiplexer #(.select(2)) multiplexer_3 (
    .in0(fourbitinverter_1_a1invert), .in1(fourbitorer_1_or1), .in2(fourbitander_1_and1),
    .in3(fourbitadder_1_sum1), .out(alu1), .sel(S));
  Multiplexer #(.select(2)) multiplexer_4 (
    .in0(fourbitinverter_1_a0invert), .in1(fourbitorer_1_or0), .in2(fourbitander_1_and0),
    .in3(fourbitadder_1_sum0), .out(alu0), .sel(S));
endmodule
