// Logisim project 4bit_adder.circ as structural Verilog: 3 circuits, main circuit HalfAdder
module HalfAdder (
  input  A,
  input  B,
  output C,
  output S
);

  and and_1 (C, A, B);
  xor xor_1 (S, A, B);
endmodule

module FullAdder (
  input  A,
  input  B,
  input  Cin,
  output S,
  output C
);

  wire halfadder_1_c, halfadder_1_s, halfadder_2_c;

  HalfAdder halfadder_1 (.A(A), .B(B), .C(halfadder_1_c), .S(halfadder_1_s));
  or or_1 (C, halfadder_2_c, halfadder_1_c);
  HalfAdder halfadder_2 (.A(halfadder_1_s), .B(Cin), .C(halfadder_2_c), .S(S));
endmodule

module FourBitAdder (
  input  A3,
  input  B3,
  input  A2,
  input  B2,
  input  A1,
  input  B1,
  input  A0,
  input  B0,
  output Carry,
  output SUM3,
  output SUM2,
  output SUM1,
  output SUM0
);

  wire fulladder_2_c, fulladder_3_c, halfadder_1_c;

  FullAdder fulladder_1 (.A(A3), .B(B3), .Cin(fulladder_2_c), .S(SUM3), .C(Carry));
  FullAdder fulladder_2 (.A(A2), .B(B2), .Cin(fulladder_3_c), .S(SUM2), .C(fulladder_2_c));
  FullAdder fulladder_3 (.A(A1), .B(B1), .Cin(halfadder_1_c), .S(SUM1), .C(fulladder_3_c));
  HalfAdder halfadder_1 (.A(A0), .B(B0), .C(halfadder_1_c), .S(SUM0));
endmodule
