// Logisim project Lab8_Common_Bus.circ as structural Verilog
module CommonBus (
  input  RB,
  input  X,
  input  Y,
  input  Z,
  input  R_W_0,
  input  Addr,
  input  [3:0] in_7,
  input  ALU,
  input  OE,
  input  R_W_1,
  input  [2:0] in_11,
  input  Copy_B_to_Bus,
  output [3:0] BUS_Observer,
  output [3:0] A,
  output [3:0] Observer_1,
  output [3:0] B,
  output [3:0] Observer_0
);

  wire and_1_out, and_2_out, and_3_out, decoder_1_out0, decoder_1_out1, decoder_1_out2, decoder_1_out3,
       not_1_out, not_2_out, not_3_out, not_4_out, undriven;
  wire [2:0] Instruction_Register_q;
  wire [3:0] controlled_buffer_1_out, controlled_buffer_8_out, controlled_buffer_12_out, fourbit_alu_1_alu0;

  Register #(.width(3)) Instruction_Register (
    .D(in_11), .en(1'b1), .clk(X), .Q(Instruction_Register_q), .clr(undriven));
  not not_1 (not_1_out, Instruction_Register_q[1]);
  not not_2 (not_2_out, Instruction_Register_q[0]);
  not not_3 (not_3_out, Instruction_Register_q[2]);
  and and_1 (and_1_out, Instruction_Register_q[2], not_1_out, not_2_out);
  and and_2 (and_2_out, Y, not_3_out);
  and and_3 (and_3_out, Z, not_3_out);
  Register #(.width(4)) Register_A (.D(in_7), .en(1'b1), .clk(and_2_out), .Q(A), .clr(and_1_out));
  Register #(.width(4)) Register_B (.D(controlled_buffer_1_out), .en(1'b1), .clk(and_3_out), .Q(B), .clr(and_1_out));
  not not_4 (not_4_out, RB);
  assign controlled_buffer_1_out = RB ? BUS_Observer : 4'bz;  // Controlled_Buffer controlled_buffer_1
  assign controlled_buffer_1_out = not_4_out ? fourbit_alu_1_alu0 : 4'bz;  // Controlled_Buffer controlled_buffer_2
  assign BUS_Observer = Copy_B_to_Bus ? B : 4'bz;  // Controlled_Buffer controlled_buffer_3
  fourbit_alu fourbit_alu_1 (
    .A(A), .B(B), .S(Instruction_Register_q[1:0]), .alu3(fourbit_alu_1_alu0[3]),
    .alu2(fourbit_alu_1_alu0[2]), .alu1(fourbit_alu_1_alu0[1]), .alu0(fourbit_alu_1_alu0[0]));  // open: Carry
  assign BUS_Observer = ALU ? fourbit_alu_1_alu0 : 4'bz;  // Controlled_Buffer controlled_buffer_4
  assign controlled_buffer_8_out[3] = decoder_1_out0 ? BUS_Observer[3] : 1'bz;  // Controlled_Buffer controlled_buffer_5
  assign controlled_buffer_8_out[2] = decoder_1_out0 ? BUS_Observer[2] : 1'bz;  // Controlled_Buffer controlled_buffer_6
  assign controlled_buffer_8_out[1] = decoder_1_out0 ? BUS_Observer[1] : 1'bz;  // Controlled_Buffer controlled_buffer_7
  assign controlled_buffer_8_out[0] = decoder_1_out0 ? BUS_Observer[0] : 1'bz;  // Controlled_Buffer controlled_buffer_8
  assign controlled_buffer_12_out[3] = decoder_1_out1 ? BUS_Observer[3] : 1'bz;  // Controlled_Buffer controlled_buffer_9
  assign controlled_buffer_12_out[2] = decoder_1_out1 ? BUS_Observer[2] : 1'bz;  // Controlled_Buffer controlled_buffer_10
  assign controlled_buffer_12_out[1] = decoder_1_out1 ? BUS_Observer[1] : 1'bz;  // Controlled_Buffer controlled_buffer_11
  assign controlled_buffer_12_out[0] = decoder_1_out1 ? BUS_Observer[0] : 1'bz;  // Controlled_Buffer controlled_buffer_12
  assign BUS_Observer[3] = decoder_1_out2 ? Observer_1[3] : 1'bz;  // Controlled_Buffer controlled_buffer_13
  assign BUS_Observer[2] = decoder_1_out2 ? Observer_1[2] : 1'bz;  // Controlled_Buffer controlled_buffer_14
  assign BUS_Observer[1] = decoder_1_out2 ? Observer_1[1] : 1'bz;  // Controlled_Buffer controlled_buffer_15
  assign BUS_Observer[0] = decoder_1_out2 ? Observer_1[0] : 1'bz;  // Controlled_Buffer controlled_buffer_16
  Decoder #(.select(2)) decoder_1 (
    .out0(decoder_1_out0), .out1(decoder_1_out1), .out2(decoder_1_out2), .out3(decoder_1_out3),
    .sel({OE, Addr}));  // open: en
  assign BUS_Observer[3] = decoder_1_out3 ? Observer_0[3] : 1'bz;  // Controlled_Buffer controlled_buffer_17
  assign BUS_Observer[2] = decoder_1_out3 ? Observer_0[2] : 1'bz;  // Controlled_Buffer controlled_buffer_18
  assign BUS_Observer[1] = decoder_1_out3 ? Observer_0[1] : 1'bz;  // Controlled_Buffer controlled_buffer_19
  assign BUS_Observer[0] = decoder_1_out3 ? Observer_0[0] : 1'bz;  // Controlled_Buffer controlled_buffer_20
  Register #(.width(4)) Memory_0 (.D(controlled_buffer_8_out), .en(1'b1), .clk(R_W_0), .Q(Observer_1), .clr(and_1_out));
  Register #(.width(4)) Memory_1 (
    .D(controlled_buffer_12_out), .en(1'b1), .clk(R_W_1), .Q(Observer_0), .clr(and_1_out));

  // Notes on the sheet:
  //   3-bit Instruction
  //   Controller
  //   Clock Cycles
  //   ALU Control
  //   4-bit Value
  //   ALU
endmodule
